# Fritzing sketch vl6180x an rp pico und circuitpython (saved by Fritzing 0.9.9b)

parts:
  Mod1 = Raspberry Pi Pico
  Bauteil1 = Adafruit VL6180 Time of Flight Sensor [part_number="Adafruit #3316"]

nets:
  N1: Mod1.pin_1, Bauteil1.SDA
  N2: Mod1.pin_2, Bauteil1.SCL
  N3: Mod1.pin_8, Mod1.pin_38, Mod1.pin_42, Bauteil1.GND
  N4: Mod1.pin_36, Bauteil1.VCC

custom parts:
  Raspberry Pi Pico: Raspberry Pi Pico. Based around the RP2040 microcontroller the Pico is a low cost microcontroller device bringing Raspberry Pi quality, cost, and easy of use to the microcontroller space. Jan 2021, Split part in to two versions: tht (this one) and SMD. This one will drill holes for a .1 in header in pcb to allow plugging in the module as well as providing pads to solder the module to the top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
  Adafruit VL6180 Time of Flight Sensor: The VL6180X (sometimes called the VL6180) is a Time of Flight distance sensor like no other you've used! The sensor contains a very tiny laser source, and a matching sensor. The VL6180X can detect the "time of flight", or how long the laser light has taken to bounce back to the sensor. Since it uses a very narrow light source, it is good for determining distance of only the surface directly in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
